# Fritzing sketch The transport schematic (saved by Fritzing 0.9.3b)

parts:
  proto1 = Adafruit_PermaProto_1_2_Board
  BUTTON1 = Arcade Button (blue)
  BUTTON2 = Arcade Button (blue)
  BUTTON3 = Arcade Button (green)
  Pro_Micro1 = Pro Micro  # not connected

nets:
  N1: proto1.connectorA5, BUTTON1.no_name_yet#1
  N2: proto1.connectorA6, BUTTON2.no_name_yet#1
  N3: proto1.connectorA7, BUTTON3.no_name_yet#1
  N4: proto1.connectorJ2, proto1.connectorZ3
  N5: proto1.connectorZ5, BUTTON1.no_name_yet#2, BUTTON2.no_name_yet#2, BUTTON3.no_name_yet#2

custom parts:
  Arcade Button (blue): Adafruit Arcade Button (blue)
  Arcade Button (green): Adafruit Arcade Button (green)
  Pro Micro: The SparkFun Pro Micro is a complete USB-based microcontoller development system, in a very small footprint, capable of implementing many types of projects. All programming can be done via the USB port.
